# Fritzing sketch deskbuddy files (saved by Fritzing 0.9.3b)

parts:
  A1 = Esp32-c3 super mini
  Sensor1 = TTP223B Capacitive Touch Sensor Module
  OLED_I2C1 = OLED 128x64 I2C Monochrome Display
  TP1 = TP4056 [chip_label=TP4056 package="DIP (Dual Inline) [THT]"]
  S1 = Toggle Switch [package=THT]
  U1 = LIPO-110mAh [package=lipo-110]

nets:
  N1: A1.Pin_4, Sensor1.SIG
  N2: A1.Pin_5, OLED_I2C1.SDA
  N3: A1.Pin_6, OLED_I2C1.SCK
  N4: A1.Pin_15, OLED_I2C1.GND
  N5: A1.Pin_16, OLED_I2C1.VDD
  N6: TP1.pin3, TP1.pin4, S1.L2, U1.+
  N7: TP1.pin5, U1.-

notes:
  EDISON SCIENCE CORNER

custom parts:
  Esp32-c3 super mini: ESP32-C3 Development Board ESP32 SuperMini Development Board ESP32 Development Board WiFi Bluetooth.
  TTP223B Capacitive Touch Sensor Module: The TTP223B capacitive touch sensor module uses the TTP223B IC. The appropriate voltage is approximately 2 to 5.5 volts.
  TP4056: A DIP stand-in part for whatever IC you want. With 6 pins on a 300mil dual inline package (DIP) footprint.
